// Logisim project Ex2.circ as structural Verilog: 1 circuit, main circuit main
module main (
  input  in_1,
  input  in_2,
  input  in_3,
  output out_4
);

  wire nor_1_out, or_1_out;

  or or_1 (or_1_out, in_1, in_2);
  nor nor_1 (nor_1_out, in_1, in_2);
  Multiplexer #(.enable("false")) multiplexer_1 (.in0(or_1_out), .in1(nor_1_out), .out(out_4), .sel(in_3));

  // Notes on the sheet:
  //   or
  //   nor
endmodule
