// Logisim project Ex2.circ as structural Verilog: 1 circuit, main circuit main
module main (
  input  in_1,
  input  in_2,
  input  in_3,
  input  in_4,
  input  in_5,
  input  in_6,
  input  in_7,
  input  in_8,
  output out_9,
  output out_10,
  output out_11,
  output out_12,
  output out_13
);

  wire and_1_out, and_2_out, and_3_out, and_4_out, and_5_out, and_6_out, and_7_out, and_8_out, and_9_out,
       and_10_out, and_11_out, and_12_out, not_1_out, not_2_out, not_3_out, not_4_out, not_5_out, not_6_out,
       not_7_out, not_8_out, or_2_out, or_3_out, or_4_out, xor_1_out, xor_3_out, xor_5_out, xor_7_out;

  and and_1 (and_1_out, in_5, or_2_out);
  not not_1 (not_1_out, in_1);
  not not_2 (not_2_out, in_1);
  or or_1 (out_9, and_1_out, and_2_out, and_3_out);
  and and_2 (and_2_out, not_1_out, or_2_out);
  and and_3 (and_3_out, not_2_out, in_5);
  xor xor_1 (xor_1_out, in_1, in_5);
  xor xor_2 (out_10, xor_1_out, or_2_out);
  and and_4 (and_4_out, in_6, or_3_out);
  not not_3 (not_3_out, in_2);
  and and_5 (and_5_out, not_3_out, or_3_out);
  not not_4 (not_4_out, in_2);
  and and_6 (and_6_out, not_4_out, in_6);
  xor xor_3 (xor_3_out, in_2, in_6);
  or or_2 (or_2_out, and_4_out, and_5_out, and_6_out);
  xor xor_4 (out_11, xor_3_out, or_3_out);
  and and_7 (and_7_out, in_7, or_4_out);
  not not_5 (not_5_out, in_3);
  not not_6 (not_6_out, in_3);
  or or_3 (or_3_out, and_7_out, and_8_out, and_9_out);
  and and_8 (and_8_out, not_5_out, or_4_out);
  and and_9 (and_9_out, not_6_out, in_7);
  xor xor_5 (xor_5_out, in_3, in_7);
  xor xor_6 (out_12, xor_5_out, or_4_out);
  and and_10 (and_10_out, in_8, 1'b0);
  not not_7 (not_7_out, in_4);
  and and_11 (and_11_out, not_7_out, 1'b0);
  not not_8 (not_8_out, in_4);
  and and_12 (and_12_out, not_8_out, in_8);
  or or_4 (or_4_out, and_10_out, and_11_out, and_12_out);
  xor xor_7 (xor_7_out, in_4, in_8);
  xor xor_8 (out_13, xor_7_out, 1'b0);
endmodule
