// Logisim project Ex3.circ as structural Verilog: 1 circuit, main circuit main
module main (
  input  _0,
  input  _1,
  input  _2,
  input  _3,
  input  _4,
  input  _0_2,
  input  _1_2,
  input  _2_2,
  input  _3_2,
  input  _4_2,
  output out_11
);

  wire xnor_1_out, xnor_2_out, xnor_3_out, xnor_4_out, xnor_5_out;

  xnor xnor_1 (xnor_1_out, _0, _0_2);
  xnor xnor_2 (xnor_2_out, _1, _1_2);
  xnor xnor_3 (xnor_3_out, _2, _2_2);
  xnor xnor_4 (xnor_4_out, _3, _3_2);
  xnor xnor_5 (xnor_5_out, _4, _4_2);
  and and_1 (out_11, xnor_1_out, xnor_2_out, xnor_3_out, xnor_4_out, xnor_5_out);

  // Notes on the sheet:
  //   DIGITOS A
  //   DIGITOS B
endmodule
