// Logisim project Ex4.circ as structural Verilog: 1 circuit, main circuit main
module main (
  input  _0,
  input  _1,
  input  _2,
  input  _3,
  input  _4,
  input  _0_2,
  input  _1_2,
  input  _2_2,
  input  _3_2,
  input  _4_2,
  output out_11
);

  wire xor_1_out, xor_2_out, xor_3_out, xor_4_out, xor_5_out;

  xor xor_1 (xor_1_out, _0, _0_2);
  xor xor_2 (xor_2_out, _1, _1_2);
  xor xor_3 (xor_3_out, _2, _2_2);
  xor xor_4 (xor_4_out, _3, _3_2);
  xor xor_5 (xor_5_out, _4, _4_2);
  or or_1 (out_11, xor_1_out, xor_2_out, xor_3_out, xor_4_out, xor_5_out);

  // Notes on the sheet:
  //   DIGITOS B
endmodule
