// Logisim project Ex5.circ as structural Verilog: 1 circuit, main circuit main
module main (
  input  in_1,
  input  in_2,
  input  in_3,
  input  in_4,
  input  in_5,
  output out_6,
  output out_7,
  output out_8,
  output out_9,
  output out_10
);

  wire and_1_out, and_2_out, and_3_out, and_4_out, and_5_out, and_6_out, and_7_out, and_8_out, and_9_out,
       and_10_out, and_11_out, and_12_out, and_13_out, and_14_out, and_15_out, not_1_out, not_2_out,
       not_3_out, not_4_out, not_5_out, or_2_out, or_3_out, or_4_out, or_5_out, xor_1_out, xor_3_out,
       xor_5_out, xor_7_out, xor_9_out;

  and and_1 (and_1_out, 1'b0, or_2_out);
  and and_2 (and_2_out, not_1_out, or_2_out);
  and and_3 (and_3_out, not_1_out, 1'b0);
  xor xor_1 (xor_1_out, not_1_out, 1'b0);
  // OR_Gate or_1 has open pins: in0=and_1_out, in1=and_2_out, in2=and_3_out, out=open
  xor xor_2 (out_6, xor_1_out, or_2_out);
  and and_4 (and_4_out, 1'b0, or_3_out);
  and and_5 (and_5_out, not_2_out, or_3_out);
  and and_6 (and_6_out, not_2_out, 1'b0);
  or or_2 (or_2_out, and_4_out, and_5_out, and_6_out);
  xor xor_3 (xor_3_out, not_2_out, 1'b0);
  xor xor_4 (out_7, xor_3_out, or_3_out);
  and and_7 (and_7_out, 1'b0, or_4_out);
  and and_8 (and_8_out, not_3_out, or_4_out);
  and and_9 (and_9_out, not_3_out, 1'b0);
  not not_1 (not_1_out, in_1);
  or or_3 (or_3_out, and_7_out, and_8_out, and_9_out);
  not not_2 (not_2_out, in_2);
  xor xor_5 (xor_5_out, not_3_out, 1'b0);
  not not_3 (not_3_out, in_3);
  xor xor_6 (out_8, xor_5_out, or_4_out);
  not not_4 (not_4_out, in_5);
  not not_5 (not_5_out, in_4);
  and and_10 (and_10_out, 1'b0, or_5_out);
  and and_11 (and_11_out, not_5_out, or_5_out);
  and and_12 (and_12_out, not_5_out, 1'b0);
  xor xor_7 (xor_7_out, not_5_out, 1'b0);
  or or_4 (or_4_out, and_10_out, and_11_out, and_12_out);
  xor xor_8 (out_9, xor_7_out, or_5_out);
  and and_13 (and_13_out, 1'b1, 1'b0);
  and and_14 (and_14_out, not_4_out, 1'b0);
  and and_15 (and_15_out, not_4_out, 1'b1);
  or or_5 (or_5_out, and_13_out, and_14_out, and_15_out);
  xor xor_9 (xor_9_out, not_4_out, 1'b1);
  xor xor_10 (out_10, xor_9_out, 1'b0);
endmodule
